// Logisim project InstructionDecoder.circ as structural Verilog
module InstructionDecoder (
  input  [4:0] rd,
  input  [4:0] rs1,
  input  [4:0] rs2,
  input  [31:0] in_4,
  input  [31:0] \const 
);

  swirl swirl_1 (
    .funct7(in_4[31:25]), .rs2(in_4[24:20]), .rs1(in_4[11:7]), .\const (\const ));  // open: funct3, rd, B, I, S, J, U, R
  OpcodeDecoder opcodedecoder_1 (
    .opcode(in_4[6:0]), .funct3(in_4[14:12]), .funct7(in_4[31:25]), .rs2(in_4[24:20]));  // open: mulh, mulsu, mulu, div, divu, op_rem, remu, mul, R, J, jal, jalr, lui, auipc, S, B, ecall, ebreak, U, sub, op_sll, op_slt, op_sltu, op_xor, op_slr, op_sra, op_or, op_and, addi, slli, slti, sltiu, xori, srli, srai, ori, andi, add, lb, lh, lw, lbu, lhu, sb, sh, sw, beq, bne, blt, bge, bltu, bgeu, I

  assign rd = in_4[11:7];
  assign rs1 = in_4[19:15];
  assign rs2 = in_4[24:20];
endmodule

module swirl (
  input  [6:0] funct7,
  input  [4:0] rs2,
  input  [4:0] rs1,
  input  [2:0] funct3,
  input  [4:0] rd,
  input  B,
  input  I,
  input  S,
  input  J,
  input  U,
  input  R,
  output [31:0] \const 
);

  wire undriven, undriven_2;
  wire [2:0] priority_encoder_1_out;
  wire [31:0] B_t, I_t, J_t, S_t;

  assign I_t = {{20{funct7[6]}}, {funct7, rs2}};  // Bit_Extender bit_extender_1
  // NoConnect on nothing
  // NoConnect on undriven
  assign B_t = {{19{funct7[6]}}, {funct7[6], rd[0], funct7[5:0], rd[4:1], 1'b0}};  // Bit_Extender bit_extender_2
  Multiplexer #(.select(3), .width(32)) multiplexer_1 (
    .in0({32{1'b0}}), .in1(B_t), .in2(I_t), .in3(S_t), .in4(J_t),
    .in5({funct7, rs2, rs1, funct3, {12{1'b0}}}), .in6({32{1'b0}}), .in7({32{1'b0}}), .out(\const ),
    .sel(priority_encoder_1_out));
  // NoConnect on nothing
  Priority_Encoder priority_encoder_1 (
    .in0(undriven), .in1(B), .in2(I), .in3(S), .in4(J), .in5(U), .in6(1'b0), .in7(R),
    .out(priority_encoder_1_out), .en_in(undriven_2));
  // NoConnect on undriven_2
  assign S_t = {{20{funct7[6]}}, {funct7, rd}};  // Bit_Extender bit_extender_3
  assign J_t = {{11{funct7[6]}}, {funct7[6], rs1, funct3, rs2[0], funct7[5:0], rs2[4:1], 1'b0}};  // Bit_Extender bit_extender_4

  // Other names for the same wires on the sheet: U_t[31:12] = {funct7, rs2, rs1, funct3};
  //   Uimm[19:0] = {funct7, rs2, rs1, funct3}

  // Notes on the sheet:
  //   const: pull=down
  //   I
  //   B
  //   S
  //   J
endmodule

module OpcodeDecoder (
  input  [6:0] opcode,
  input  [2:0] funct3,
  input  [6:0] funct7,
  input  [4:0] rs2,
  output add,
  output mul,
  output sub,
  output mulh,
  output R,
  output op_sll,
  output mulsu,
  output op_slt,
  output mulu,
  output op_sltu,
  output div,
  output op_xor,
  output divu,
  output op_slr,
  output op_rem,
  output op_sra,
  output remu,
  output op_or,
  output op_and,
  output addi,
  output slli,
  output slti,
  output sltiu,
  output xori,
  output srli,
  output srai,
  output ori,
  output andi,
  output I,
  output lb,
  output lh,
  output lw,
  output lbu,
  output lhu,
  output sb,
  output S,
  output sh,
  output sw,
  output beq,
  output bne,
  output blt,
  output B,
  output bge,
  output bltu,
  output bgeu,
  output J,
  output jal,
  output jalr,
  output lui,
  output U,
  output auipc,
  output ecall,
  output ebreak
);

  wire and_14_out, compare7bits_2_equal, compare7bits_3_equal, compare7bits_10_equal, compare7bits_11_equal,
       compare7bits_12_equal, compare7bits_13_equal, demultiplexer_2_out0, demultiplexer_2_out1,
       demultiplexer_2_out2, demultiplexer_2_out3, demultiplexer_2_out4, demultiplexer_2_out5,
       demultiplexer_2_out6, demultiplexer_2_out7, demultiplexer_3_out1, demultiplexer_3_out5,
       demultiplexer_4_out3, demultiplexer_4_out6, demultiplexer_4_out7, demultiplexer_5_out3,
       demultiplexer_5_out4, demultiplexer_5_out5, demultiplexer_5_out6, demultiplexer_5_out7,
       demultiplexer_6_out2, demultiplexer_6_out3;

  compare7bits compare7bits_1 (.A(7'b0110011), .B(opcode), .equal(R));
  compare7bits compare7bits_2 (.A(opcode), .B(7'b0010011), .equal(compare7bits_2_equal));
  compare7bits compare7bits_3 (.A(opcode), .B(7'b0000011), .equal(compare7bits_3_equal));
  compare7bits compare7bits_4 (.A(opcode), .B(7'b0100011), .equal(S));
  compare7bits compare7bits_5 (.A(7'b1100011), .B(opcode), .equal(B));
  compare7bits compare7bits_6 (.A(7'b1101111), .B(opcode), .equal(J));
  compare7bits compare7bits_7 (.A(7'b1100111), .B(opcode), .equal(jalr));
  compare7bits compare7bits_8 (.A(7'b0110111), .B(opcode), .equal(lui));
  compare7bits compare7bits_9 (.A(7'b0010111), .B(opcode), .equal(auipc));
  compare7bits compare7bits_10 (.A(7'b1110011), .B(opcode), .equal(compare7bits_10_equal));
  Demultiplexer demultiplexer_1 (.out0(ecall), .out1(ebreak), .in(compare7bits_10_equal), .sel(rs2[0]));
  Demultiplexer #(.select(3)) demultiplexer_2 (
    .out0(demultiplexer_2_out0), .out1(demultiplexer_2_out1), .out2(demultiplexer_2_out2),
    .out3(demultiplexer_2_out3), .out4(demultiplexer_2_out4), .out5(demultiplexer_2_out5),
    .out6(demultiplexer_2_out6), .out7(demultiplexer_2_out7), .in(R), .sel(funct3));
  compare7bits compare7bits_11 (.A({7{1'b0}}), .B(funct7), .equal(compare7bits_11_equal));
  compare7bits compare7bits_12 (.A(funct7), .B(7'b0100000), .equal(compare7bits_12_equal));
  Demultiplexer #(.select(3)) demultiplexer_3 (
    .out0(addi), .out1(demultiplexer_3_out1), .out2(slti), .out3(sltiu), .out4(xori),
    .out5(demultiplexer_3_out5), .out6(ori), .out7(andi), .in(compare7bits_2_equal), .sel(funct3));
  // NoConnect on demultiplexer_4_out3
  Demultiplexer #(.select(3)) demultiplexer_4 (
    .out0(lb), .out1(lh), .out2(lw), .out3(demultiplexer_4_out3), .out4(lbu), .out5(lhu),
    .out6(demultiplexer_4_out6), .out7(demultiplexer_4_out7), .in(compare7bits_3_equal), .sel(funct3));
  // NoConnect on demultiplexer_4_out6
  // NoConnect on demultiplexer_4_out7
  // NoConnect on demultiplexer_5_out3
  // NoConnect on demultiplexer_5_out4
  Demultiplexer #(.select(3)) demultiplexer_5 (
    .out0(sb), .out1(sh), .out2(sw), .out3(demultiplexer_5_out3), .out4(demultiplexer_5_out4),
    .out5(demultiplexer_5_out5), .out6(demultiplexer_5_out6), .out7(demultiplexer_5_out7), .in(S),
    .sel(funct3));
  // NoConnect on demultiplexer_5_out5
  // NoConnect on demultiplexer_5_out6
  // NoConnect on demultiplexer_5_out7
  // NoConnect on demultiplexer_6_out2
  // NoConnect on demultiplexer_6_out3
  Demultiplexer #(.select(3)) demultiplexer_6 (
    .out0(beq), .out1(bne), .out2(demultiplexer_6_out2), .out3(demultiplexer_6_out3), .out4(blt), .out5(bge),
    .out6(bltu), .out7(bgeu), .in(B), .sel(funct3));
  or or_1 (U, lui, auipc);
  and and_1 (add, demultiplexer_2_out0, compare7bits_11_equal);
  and and_2 (sub, demultiplexer_2_out0, compare7bits_12_equal);
  and and_3 (op_sll, demultiplexer_2_out1, compare7bits_11_equal);
  and and_4 (op_slt, demultiplexer_2_out2, compare7bits_11_equal);
  and and_5 (op_sltu, demultiplexer_2_out3, compare7bits_11_equal);
  and and_6 (op_xor, demultiplexer_2_out4, compare7bits_11_equal);
  and and_7 (op_slr, demultiplexer_2_out5, compare7bits_11_equal);
  and and_8 (op_sra, demultiplexer_2_out5, compare7bits_12_equal);
  and and_9 (op_or, demultiplexer_2_out6, compare7bits_11_equal);
  and and_10 (op_and, demultiplexer_2_out7, compare7bits_11_equal);
  and and_11 (slli, compare7bits_11_equal, demultiplexer_3_out1);
  and and_12 (srli, demultiplexer_3_out5, compare7bits_11_equal);
  and and_13 (srai, demultiplexer_3_out5, compare7bits_12_equal);
  and and_14 (and_14_out, R, compare7bits_13_equal);
  or or_2 (I, compare7bits_2_equal, compare7bits_3_equal, jalr, compare7bits_10_equal);
  Demultiplexer #(.select(3)) demultiplexer_7 (
    .out0(mul), .out1(mulh), .out2(mulsu), .out3(mulu), .out4(div), .out5(divu), .out6(op_rem), .out7(remu),
    .in(and_14_out), .sel(funct3));
  compare7bits compare7bits_13 (.A(7'b0000001), .B(funct7), .equal(compare7bits_13_equal));

  assign jal = J;
endmodule

module compare7bits (
  input  [6:0] A,
  input  [6:0] B,
  output equal
);

  wire [6:0] xnor_1_out;

  assign xnor_1_out = ~(A ^ B);  // XNOR_Gate xnor_1, 7 bits wide
  and and_1 (equal, xnor_1_out[0], xnor_1_out[1], xnor_1_out[2], xnor_1_out[3], xnor_1_out[4], xnor_1_out[5], xnor_1_out[6]);
endmodule
